# Fritzing sketch power (saved by Fritzing 0.9.1b)

parts:
  Part1 = Adafruit FONA - Mini Cellular GSM Breakout
  Part2 = PowerBoost 500 Basic
  BATT1 = LiPoly Battery (1300mAh)
  U2 = SWITCH_SPDT [package=kps-1290]
  Raspberry_Pi1 = Raspberry Pi B+

nets:
  N1: Part1.GND, BATT1.negative
  N2: Part1.VBAT#56, BATT1.positive
  N3: Part1.PWRKEY_5V, Raspberry_Pi1.GPIO21
  N4: Part1.VBAT#107, Part2.VBAT
  GND: Part2.GND, U2.O, Raspberry_Pi1.GND
  N5: Part2.ENABLE, U2.S
  N6: Part2.5.0V, Raspberry_Pi1.5V

custom parts:
  Adafruit FONA - Mini Cellular GSM Breakout: An all-in-one cellular phone module that lets you add voice, text, SMS and GPRS data to your project. Quad-band 850/900/1800/1900MHz - connect onto any global GSM network with any 2G SIM. Includes an onboard LiPoly battery charging circuitry so you can take your project on the go. Also works as an FM radio receiver.
  PowerBoost 500 Basic: The PowerBoost 500 Basic is a little DC/DC boost converter module that can run from 1.8V batteries or higher, and convert the battery output to 5.2V DC for running your 5V projects. At its heart is a TPS61090 boost converter from TI. This boost converter chip has some really nice extras such as low battery detection, 2A internal switch, synchronous conversion, excellent efficiency, and 700KHz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
  LiPoly Battery (1300mAh): Lithium Ion Polymer Battery (1300mAh)
